// Logisim project 龙少的8位单周期.circ as structural Verilog: 4 circuits, main circuit main
module main (
  input  [7:0] in_1,
  input  [7:0] in_2,
  input  in_3,
  input  in_4,
  input  in_5,
  input  [7:0] in_6,
  input  in_7,
  input  [7:0] in_8
);

  wire n74181_1_cn_4, n74181_2_cn_4;
  wire [3:0] n74181_1_y, n74181_2_y;
  wire [7:0] ram_1_data, register_1_q, register_2_q, register_3_q;

  Register register_1 (.Q(register_1_q));  // open: D, en, clk, clr
  Register register_2 (.Q(register_2_q));  // open: D, en, clk, clr
  Register register_3 (.Q(register_3_q));  // open: D, en, clk, clr
  // Probe on ram_1_data
  RAM #(.bus("separate")) ram_1 (
    .addr(in_1), .din(in_2), .data(ram_1_data), .str(in_3), .clk(in_4), .ld(in_5));  // open: sel, clr
  _74181 u_74181_1 (
    .Cn_4(n74181_1_cn_4), .S0_S3(register_3_q[7:4]), .A(register_1_q[3:0]), .B(register_2_q[3:0]),
    .Y(n74181_1_y), .Cn(register_3_q[2]), .M(register_3_q[3]));  // open: A_B, P, G
  _74181 u_74181_2 (
    .Cn_4(n74181_2_cn_4), .S0_S3(register_3_q[7:4]), .A(register_1_q[7:4]), .B(register_2_q[7:4]),
    .Y(n74181_2_y), .Cn(n74181_1_cn_4), .M(register_3_q[3]));  // open: A_B, P, G
  Register register_4 (.D({n74181_2_y, n74181_1_y}), .clk(in_7));  // open: en, Q, clr
endmodule

module _74181 (
  input  Cn,
  input  M,
  input  [3:0] S0_S3,
  input  [3:0] A,
  input  [3:0] B,
  output [3:0] Y,
  output A_B,
  output Cn_4,
  output P,
  output G
);

  wire and_1_out, and_3_out, and_4_out, and_5_out, and_6_out, and_7_out, and_8_out, and_9_out, and_10_out,
       and_11_out, and_12_out, and_13_out, and_14_out, and_15_out, and_16_out, and_17_out, and_18_out,
       and_19_out, and_20_out, and_21_out, and_22_out, and_23_out, and_24_out, and_25_out, and_26_out,
       and_27_out, and_28_out, and_29_out, and_30_out, and_31_out, and_32_out, nand_2_out, nor_3_out,
       nor_4_out, nor_5_out, nor_6_out, nor_7_out, nor_8_out, nor_9_out, nor_10_out, nor_11_out, nor_12_out,
       nor_13_out, not_1_out, not_2_out, not_3_out, not_4_out, not_5_out, xor_2_out, xor_4_out, xor_6_out;

  Pull_Resistor #(.pull(1)) pull_resistor_1 (.node(A_B));
  and and_1 (and_1_out, P, G);
  nor nor_1 (Cn_4, and_1_out, and_3_out);
  nor nor_2 (G, and_4_out, and_5_out, and_6_out, nor_4_out);
  and and_2 (A_B, Y[0], Y[1], Y[2], Y[3]);
  and and_3 (and_3_out, ~Cn, G);  // AND_Gate
  nand nand_1 (P, nor_11_out, nor_8_out, nor_5_out, nor_3_out);
  and and_4 (and_4_out, nor_13_out, nor_8_out, nor_5_out, nor_3_out);
  and and_5 (and_5_out, nor_9_out, nor_5_out, nor_3_out);
  and and_6 (and_6_out, nor_3_out, nor_7_out);
  and and_7 (and_7_out, B[3], S0_S3[3], A[3]);
  nor nor_3 (nor_3_out, and_7_out, and_8_out);
  and and_8 (and_8_out, S0_S3[2], A[3], not_1_out);
  and and_9 (and_9_out, not_1_out, S0_S3[1]);
  not not_1 (not_1_out, B[3]);
  nor nor_4 (nor_4_out, and_9_out, and_10_out, A[3]);
  and and_10 (and_10_out, S0_S3[0], B[3]);
  xor xor_1 (Y[3], xor_2_out, nor_6_out);
  xor xor_2 (xor_2_out, nor_3_out, nor_4_out);
  and and_11 (and_11_out, nor_5_out, nor_8_out, nor_11_out, Cn, not_5_out);
  nor nor_5 (nor_5_out, and_13_out, and_12_out);
  and and_12 (and_12_out, S0_S3[2], A[2], not_2_out);
  and and_13 (and_13_out, B[2], S0_S3[3], A[2]);
  nor nor_6 (nor_6_out, and_11_out, and_14_out, and_17_out, and_18_out);
  and and_14 (and_14_out, nor_13_out, nor_5_out, nor_8_out, not_5_out);
  nor nor_7 (nor_7_out, and_15_out, and_16_out, A[2]);
  and and_15 (and_15_out, not_2_out, S0_S3[1]);
  and and_16 (and_16_out, S0_S3[0], B[2]);
  not not_2 (not_2_out, B[2]);
  and and_17 (and_17_out, nor_9_out, nor_5_out, not_5_out);
  and and_18 (and_18_out, nor_7_out, not_5_out);
  nor nor_8 (nor_8_out, and_20_out, and_19_out);
  and and_19 (and_19_out, S0_S3[2], A[1], not_3_out);
  and and_20 (and_20_out, B[1], S0_S3[3], A[1]);
  xor xor_3 (Y[2], xor_4_out, nor_10_out);
  xor xor_4 (xor_4_out, nor_5_out, nor_7_out);
  and and_21 (and_21_out, nor_8_out, nor_11_out, Cn, not_5_out);
  nor nor_9 (nor_9_out, and_22_out, and_23_out, A[1]);
  and and_22 (and_22_out, not_3_out, S0_S3[1]);
  and and_23 (and_23_out, S0_S3[0], B[1]);
  not not_3 (not_3_out, B[1]);
  nor nor_10 (nor_10_out, and_21_out, and_25_out, and_24_out);
  and and_24 (and_24_out, nor_9_out, not_5_out);
  and and_25 (and_25_out, nor_13_out, nor_8_out, not_5_out);
  and and_26 (and_26_out, B[0], S0_S3[3], A[0]);
  xor xor_5 (Y[1], xor_6_out, nor_12_out);
  xor xor_6 (xor_6_out, nor_8_out, nor_9_out);
  and and_27 (and_27_out, nor_11_out, Cn, not_5_out);
  nor nor_11 (nor_11_out, and_26_out, and_29_out);
  and and_28 (and_28_out, not_4_out, S0_S3[1]);
  and and_29 (and_29_out, S0_S3[2], A[0], not_4_out);
  not not_4 (not_4_out, B[0]);
  and and_30 (and_30_out, nor_11_out, ~nor_13_out);  // AND_Gate
  nor nor_12 (nor_12_out, and_27_out, and_31_out);
  and and_31 (and_31_out, nor_13_out, not_5_out);
  nor nor_13 (nor_13_out, and_28_out, and_32_out, A[0]);
  and and_32 (and_32_out, S0_S3[0], B[0]);
  xor xor_7 (Y[0], and_30_out, nand_2_out);
  nand nand_2 (nand_2_out, Cn, not_5_out);
  not not_5 (not_5_out, M);
endmodule

module ALU (
  input  in_1,
  input  [7:0] ROM_DB0_7,
  input  [7:0] ROM_DB8_15,
  input  in_4,
  input  clk,
  input  [7:0] in_6,
  input  clr
);

  wire A, A0, A1, A2, A__0, A__0_t, A__0_t_t, A__7, A__A, A__B, A_C, ALU_O, and_2_out, and_3_out, and_4_out,
       and_8_out, B, B__0, B__0_t, B__A, B__B, clk0, clk1, clk2, clk3, clock_1_out, decoder_5_out6,
       decoder_5_out7, JC, jmp, JNH_A, JNH_B, n74181_1_a_b, n74181_1_cn_4, n74181_2_a_b, n74181_2_cn_4,
       N_A_B, nand_1_out, nand_3_out, nand_4_out, nO, NOP2, NOP5, nor_1_out, nor_2_out, not_1_out, not_2_out,
       not_3_out, not_4_out, or_1_out, or_2_out, or_3_out, or_4_out, or_5_out, or_6_out, or_7_out, or_8_out,
       RAM_RD, RAM_WR;
  wire [1:0] counter_1_q;
  wire [3:0] register_2_q, register_3_q;
  wire [3:3] not_6_out;
  wire [6:0] not_8_out;
  wire [7:0] A_q, and_5_out, B_q, bit_extender_1_out, DB_q, decoder_2_out0, decoder_3_out0, decoder_4_out0,
       IR_q, n74181_1_y, not_7_out, pull_resistor_1_node, rom_1_data, rom_2_data;
  wire [7:7] and_1_out;
  wire [17:0] PC;
  wire [23:0] RAM_AB;
  wire [23:18] PC_q;

  Clock clock_1 (.out(clock_1_out));
  Decoder #(.select(2), .disabled(0), .enable("false")) decoder_1 (
    .out0(clk0), .out1(clk1), .out2(clk2), .out3(clk3), .sel(counter_1_q));
  Counter #(.width(2), .max('h3)) counter_1 (
    .Q(counter_1_q), .clk(clock_1_out), .clr(clr));  // open: load, D, count, carry
  or or_1 (or_1_out, RAM_AB[22], RAM_AB[23]);
  ROM #(.addrWidth(18)) rom_1 (.addr(PC), .data(rom_1_data));  // open: sel
  Register DB (.D(rom_1_data), .Q(DB_q), .clk(clk0), .clr(clr));  // open: en
  nor nor_1 (nor_1_out, RAM_RD, or_1_out);
  nor nor_2 (nor_2_out, or_1_out, RAM_WR);
  Pull_Resistor pull_resistor_1 (.node(pull_resistor_1_node));
  assign pull_resistor_1_node = not_1_out ? DB_q : 8'bz;  // Controlled_Buffer controlled_buffer_1
  not not_1 (not_1_out, nO);
  RAM #(.addrWidth(19)) ram_1 (
    .addr(RAM_AB[18:0]), .data(pull_resistor_1_node), .clk(nor_2_out), .ld(nor_1_out), .clr(clr));  // open: sel
  assign pull_resistor_1_node = nand_1_out ? {A_q[6:0], A__0_t_t} : 8'bz;  // Controlled_Buffer controlled_buffer_2
  Register u_A (.D(pull_resistor_1_node), .Q(A_q), .clk(A), .clr(clr));  // open: en
  assign pull_resistor_1_node = A_C ? {A__7, A_q[7:1]} : 8'bz;  // Controlled_Buffer controlled_buffer_3
  assign pull_resistor_1_node = B__0 ? {B_q[6:0], 1'b0} : 8'bz;  // Controlled_Buffer controlled_buffer_4
  Register u_B (.D(pull_resistor_1_node), .Q(B_q), .clk(B), .clr(clr));  // open: en
  assign pull_resistor_1_node = nand_3_out ? {and_1_out[7], B_q[7:1]} : 8'bz;  // Controlled_Buffer controlled_buffer_5
  Register u_A0 (.D(pull_resistor_1_node), .Q(RAM_AB[7:0]), .clk(A0), .clr(clr));  // open: en
  Register u_A1 (.D(pull_resistor_1_node), .Q(RAM_AB[15:8]), .clk(A1), .clr(clr));  // open: en
  Register u_A2 (.D(pull_resistor_1_node), .Q(RAM_AB[23:16]), .clk(A2), .clr(clr));  // open: en
  not not_2 (not_2_out, and_3_out);
  Register register_1 (.D(n74181_1_y), .clk(in_1));  // open: en, Q, clr
  _74181 u_74181_1 (
    .A_B(n74181_1_a_b), .Cn_4(n74181_1_cn_4), .S0_S3(DB_q[7:4]), .A(A_q[3:0]), .B(B_q[3:0]),
    .Y(n74181_1_y[3:0]), .Cn(DB_q[2]), .M(DB_q[3]));  // open: P, G
  _74181 u_74181_2 (
    .A_B(n74181_2_a_b), .Cn_4(n74181_2_cn_4), .S0_S3(DB_q[7:4]), .A(A_q[7:4]), .B(B_q[7:4]),
    .Y(n74181_1_y[7:4]), .Cn(n74181_1_cn_4), .M(DB_q[3]));  // open: P, G
  Counter #(.width(24), .max('hffffff)) u_PC (
    .load(not_2_out), .D(RAM_AB), .count(and_3_out), .Q({PC_q, PC}), .clk(clk0), .clr(clr));  // open: carry
  nand nand_1 (nand_1_out, A__A, A__0_t);
  nand nand_2 (A_C, A__B, A__0);
  assign pull_resistor_1_node = ALU_O ? n74181_1_y : 8'bz;  // Controlled_Buffer controlled_buffer_6
  and and_1 (and_1_out[7], or_8_out, or_7_out, B__0_t);
  nand nand_3 (nand_3_out, B__0_t, B__B, B__A);
  or or_2 (or_2_out, n74181_2_a_b, n74181_1_a_b);
  or or_3 (or_3_out, or_2_out, N_A_B);
  or or_4 (or_4_out, n74181_2_cn_4, JC);
  or or_5 (or_5_out, B_q[7], JNH_B);
  and and_2 (and_2_out, or_5_out, or_6_out);
  or or_6 (or_6_out, A_q[7], JNH_A);
  or or_7 (or_7_out, B_q[7], B__B);
  or or_8 (or_8_out, A_q[0], B__A);
  and and_3 (and_3_out, or_3_out, or_4_out, and_4_out);
  and and_4 (and_4_out, and_2_out, jmp);
  ROM #(.addrWidth(18)) rom_2 (.addr(PC), .data(rom_2_data));  // open: sel
  assign bit_extender_1_out = {{7{and_3_out}}, and_3_out};  // Bit_Extender bit_extender_1
  assign and_5_out = bit_extender_1_out & {IR_q[0], IR_q[1], IR_q[2], IR_q[3], IR_q[4], IR_q[5], IR_q[6], IR_q[7]};  // AND_Gate and_5, 8 bits wide
  nand nand_4 (nand_4_out, IR_q[3], IR_q[0], IR_q[1], IR_q[2], IR_q[4], IR_q[5], IR_q[6], IR_q[7]);
  Register IR (.D(rom_2_data), .Q(IR_q), .clk(clk0), .clr(clr));  // open: en
  and and_6 (A__0_t_t, A_q[7], A__0_t);
  and and_7 (A__7, B_q[7], A__0);
  Register #(.width(4)) register_2 (.D(and_5_out[3:0]), .Q(register_2_q), .clk(clk1), .clr(clr));  // open: en
  Register #(.width(4)) register_3 (.D(and_5_out[7:4]), .Q(register_3_q), .clk(and_8_out), .clr(clr));  // open: en
  and and_8 (and_8_out, clk2, nand_4_out);
  Decoder #(.select(3), .disabled(0)) decoder_2 (
    .out0(decoder_2_out0[0]), .out1(decoder_2_out0[1]), .out2(decoder_2_out0[2]), .out3(decoder_2_out0[3]),
    .out4(decoder_2_out0[4]), .out5(decoder_2_out0[5]), .out6(decoder_2_out0[6]), .out7(decoder_2_out0[7]),
    .sel({register_2_q[1], register_2_q[2], register_2_q[3]}), .en(register_2_q[0]));
  not not_3 (not_3_out, register_2_q[0]);
  Decoder #(.select(3), .disabled(0)) decoder_3 (
    .out0(decoder_3_out0[0]), .out1(decoder_3_out0[1]), .out2(decoder_3_out0[2]), .out3(decoder_3_out0[3]),
    .out4(decoder_3_out0[4]), .out5(decoder_3_out0[5]), .out6(decoder_3_out0[6]), .out7(decoder_3_out0[7]),
    .sel({register_2_q[1], register_2_q[2], register_2_q[3]}), .en(not_3_out));
  Decoder #(.select(3), .disabled(0)) decoder_4 (
    .out0(decoder_4_out0[0]), .out1(decoder_4_out0[1]), .out2(decoder_4_out0[2]), .out3(decoder_4_out0[3]),
    .out4(decoder_4_out0[4]), .out5(decoder_4_out0[5]), .out6(decoder_4_out0[6]), .out7(decoder_4_out0[7]),
    .sel({register_3_q[1], register_3_q[2], register_3_q[3]}), .en(register_3_q[0]));
  not not_4 (not_4_out, register_3_q[0]);
  Decoder #(.select(3), .disabled(0)) decoder_5 (
    .out1(A), .out2(B), .out3(A0), .out4(A1), .out5(A2), .out6(decoder_5_out6), .out7(decoder_5_out7),
    .sel({register_3_q[1], register_3_q[2], register_3_q[3]}), .en(not_4_out));  // open: out0
  not not_5 (RAM_WR, decoder_5_out7);
  assign {A__0, B__A, B__B, B__0_t, not_6_out[3], A__A, A__0_t, A__B} = ~decoder_2_out0;  // NOT_Gate not_6, 8 bits wide
  assign {not_7_out[7:4], nO, RAM_RD, not_7_out[1:0]} = ~decoder_3_out0;  // NOT_Gate not_7, 8 bits wide
  assign {NOP5, not_8_out[6], jmp, JC, N_A_B, JNH_B, JNH_A, not_8_out[0]} = ~decoder_4_out0;  // NOT_Gate not_8, 8 bits wide
  not not_9 (NOP2, decoder_5_out6);
  not not_10 (B__0, not_6_out[3]);
  not not_11 (ALU_O, not_7_out[1]);

  // Notes on the sheet:
  //   U8
  //   contents of rom_1 (hex, n*v repeats v):
  //   0 0 9 ff c0 80 ff ff ff c0 0 c ff 6 1 0 15 ff 0 1 0 16 ff 0 1 0 17 ff 2 1 0 18 ff 0 1 0 19 ff 4 1 0
  //   1a ff 0 1 0 1b ff 7 1 0 1c ff 0 1 0 1d ff 9 1 0 1e ff 0 1 0 1f ff b 1 0 20 ff 0 1 0 21 ff d 1 0 22
  //   ff 0 1 0 23 ff 10 1 0 24 ff 0 1 0 25 ff 12 1 0 26 ff 0 1 0 27 ff 14 1 0 28 ff 0 1 0 29 ff 16 1 0 2a
  //   ff 0 1 0 2b ff 18 1 0 2c ff 0 1 0 2d ff 1b 1 0 2e ff 0 1 0 2f ff 1d 1 0 30 ff 0 1 0 31 ff 1f 1 0 32
  //   ff 0 1 0 33 ff 21 1 0 34 ff 0 1 0 35 ff 23 1 0 36 ff 0 1 0 37 ff 25 1 0 38 ff 0 1 0 39 ff 28 1 0 3a
  //   ff 0 1 0 3b ff 2a 1 0 3c ff 0 1 0 3d ff 2c 1 0 3e ff 0 1 0 3f ff 2e 1 0 40 ff 0 1 0 41 ff 30 1 0 42
  //   ff 0 1 0 43 ff 32 1 0 44 ff 0 1 0 45 ff 34 1 0 46 ff 0 1 0 47 ff 36 1 0 48 ff 0 1 0 49 ff 38 1 0 4a
  //   ff 0 1 0 4b ff 3a 1 0 4c ff 0 1 0 4d ff 3c 1 0 4e ff 0 1 0 4f ff 3e 1 0 50 ff 0 1 0 51 ff 40 1 0 52
  //   ff 0 1 0 53 ff 42 1 0 54 ff 0 1 0 55 ff 44 1 0 56 ff 0 1 0 57 ff 46 1 0 58 ff 0 1 0 59 ff 48 1 0 5a
  //   ff 0 1 0 5b ff 49 1 0 5c ff 0 1 0 5d ff 4b 1 0 5e ff 0 1 0 5f ff 4d 1 0 60 ff 0 1 0 61 ff 4f 1 0 62
  //   ff 0 1 0 63 ff 51 1 0 64 ff 0 1 0 65 ff 52 1 0 66 ff 0 1 0 67 ff 54 1 0 68 ff 0 1 0 69 ff 56 1 0 6a
  //   ff 0 1 0 6b ff 57 1 0 6c ff 0 1 0 6d ff 59 1 0 6e ff 0 1 0 6f ff 5a 1 0 70 ff 0 1 0 71 ff 5c 1 0 72
  //   ff 0 1 0 73 ff 5e 1 0 74 ff 0 1 0 75 ff 5f 1 0 76 ff 0 1 0 77 ff 61 1 0 78 ff 0 1 0 79 ff 62 1 0 7a
  //   ff 0 1 0 7b ff 63 1 0 7c ff 0 1 0 7d ff 65 1 0 7e ff 0 1 0 7f ff 66 1 0 80 ff 0 1 0 81 ff 68 1 0 82
  //   ff 0 1 0 83 ff 69 1 0 84 ff 0 1 0 85 ff 6a 1 0 86 ff 0 1 0 87 ff 6b 1 0 88 ff 0 1 0 89 ff 6d 1 0 8a
  //   ff 0 1 0 8b ff 6e 1 0 8c ff 0 1 0 8d ff 6f 1 0 8e ff 0 1 0 8f ff 70 1 0 90 ff 0 1 0 91 ff 71 1 0 92
  //   ff 0 1 0 93 ff 72 1 0 94 ff 0 1 0 95 ff 73 1 0 96 ff 0 1 0 97 ff 74 1 0 98 ff 0 1 0 99 ff 75 1 0 9a
  //   ff 0 1 0 9b ff 76 1 0 9c ff 0 1 0 9d ff 77 1 0 9e ff 0 1 0 9f ff 78 1 0 a0 ff 0 1 0 a1 ff 78 1 0 a2
  //   ff 0 1 0 a3 ff 79 1 0 a4 ff 0 1 0 a5 ff 7a 1 0 a6 ff 0 1 0 a7 ff 7a 1 0 a8 ff 0 1 0 a9 ff 7b 1 0 aa
  //   ff 0 1 0 ab ff 7c 1 0 ac ff 0 1 0 ad ff 7c 1 0 ae ff 0 1 0 af ff 7d 1 0 b0 ff 0 1 0 b1 ff 7d 1 0 b2
  //   ff 0 1 0 b3 ff 7e 1 0 b4 ff 0 1 0 b5 ff 7e 1 0 b6 ff 0 1 0 b7 ff 7e 1 0 b8 ff 0 1 0 b9 ff 7f 1 0 ba
  //   ff 0 1 0 bb ff 7f 1 0 bc ff 0 1 0 bd ff 7f 1 0 be ff 0 1 0 bf ff 7f 1 0 c0 ff 0 1 0 c1 ff 80 1 0 c2
  //   ff 0 1 0 c3 ff 80 1 0 c4 ff 0 1 0 c5 ff 80 1 0 c6 ff 0 1 0 c7 ff 80 1 0 c8 ff 0 1 0 c9 ff 80 1 0 ca
  //   ff 0 0 3b 31 ff 1 6 74 ff 0 1 6 75 ff 0 1 6 78 ff 2 0 1 6 75 ff ff 1 6 77 ff 94 0 3 c2 94 0 3 c8 ff
  //   1 6 78 ff ff 0 0 1 6 74 ff ff 1 6 76 ff 94 0 3 db 94 0 3 ef ff 1 6 77 ff ff 0 0 3 e9 0 0 3 ef ff 1 6
  //   78 ff ff 0 1 6 75 ff ff 1 6 79 ff ff 1 6 7a ff 0 1 6 79 ff ff ff 1 6 7b ff bf 1 6 7a ff ff 0 1 6 7c
  //   ff bf 1 6 74 ff ff ff 1 6 7d ff bf 1 6 75 ff ff 0 1 6 7e ff bf 1 6 7c ff ff 1 0 4 ff ff 1 6 7b ff ff
  //   1 0 5 ff ff 1 6 7e ff ff 1 0 6 ff ff 1 6 7d ff ff 1 0 7 ff ff 1 0 a ff f 1 0 8 ff ff 1 0 9 ff ff ff
  //   1 0 8 ff ff 1 0 6 ff ff 1 0 7 ff ff ff 1 0 6 ff ff 0 4 9f ff 1 0 4 ff ff 1 0 8 ff ff 94 1 0 5 ff ff
  //   1 0 9 ff ff 94 0 4 99 94 0 4 9f ff 1 0 8 ff ff 0 1 0 a ff ff f4 0 4 57 f4 1 0 8 ff ff 1 6 80 ff ff 1
  //   0 9 ff ff 1 6 7f ff ff 1 6 7f ff ff 1 6 77 ff ff 1 6 76 ff ff 0 af ff ff 1 6 78 ff ff 1 6 76 ff ff 0
  //   af 4*ff af 1 6 74 ff ff 0 0 4 ef 0 0 4 f5 ff 1 6 75 ff ff 0 1 6 75 ff ff 0 5 b f4 1 6 74 ff ff 0 5 b
  //   f4 0 5 f ff 0 3 aa ff 1 6 78 ff 3 0 1 6 75 ff ff 1 6 77 ff 94 0 5 27 94 0 5 2d ff 1 6 78 ff ff 0 0 1
  //   6 74 ff ff 1 6 76 ff 94 0 5 40 94 0 5 54 ff 1 6 77 ff ff 0 0 5 4e 0 0 5 54 ff 1 6 78 ff ff 0 1 6 75
  //   ff ff 1 6 79 ff ff 1 6 7a ff 0 1 6 79 ff ff ff 1 6 7b ff bf 1 6 7a ff ff 0 1 6 7c ff bf 1 6 74 ff ff
  //   ff 1 6 7d ff bf 1 6 75 ff ff 0 1 6 7e ff bf 1 6 7c ff ff 1 0 4 ff ff 1 6 7b ff ff 1 0 5 ff ff 1 6 7e
  //   ff ff 1 0 6 ff ff 1 6 7d ff ff 1 0 7 ff ff 1 0 a ff f 1 0 8 ff ff 1 0 9 ff ff ff 1 0 8 ff ff 1 0 6
  //   ff ff 1 0 7 ff ff ff 1 0 6 ff ff 0 6 4 ff 1 0 4 ff ff 1 0 8 ff ff 94 1 0 5 ff ff 1 0 9 ff ff 94 0 5
  //   fe 94 0 6 4 ff 1 0 8 ff ff 0 1 0 a ff ff f4 0 5 bc f4 1 0 8 ff ff 1 6 80 ff ff 1 0 9 ff ff 1 6 7f ff
  //   ff 1 6 80 ff ff 1 6 81 ff ff 1 6 82 ff 0 1 6 81 ff ff 1 6 77 ff ff 1 6 76 ff ff 0 af ff ff 1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
  //   DB
  //   U4
  //   contents of rom_2 (hex, n*v repeats v):
  //   35 34 33 d 35 33 ff 37 ff 35 34 33 ff 37 35 34 33 ff 37 35 34 33 ff 37 35 34 33 ff 37 35 34 33 ff 37
  //   35 34 33 ff 37 35 34 33 ff 37 35 34 33 ff 37 35 34 33 ff 37 35 34 33 ff 37 35 34 33 ff 37 35 34 33
  //   ff 37 35 34 33 ff 37 35 34 33 ff 37 35 34 33 ff 37 35 34 33 ff 37 35 34 33 ff 37 35 34 33 ff 37 35
  //   34 33 ff 37 35 34 33 ff 37 35 34 33 ff 37 35 34 33 ff 37 35 34 33 ff 37 35 34 33 ff 37 35 34 33 ff
  //   37 35 34 33 ff 37 35 34 33 ff 37 35 34 33 ff 37 35 34 33 ff 37 35 34 33 ff 37 35 34 33 ff 37 35 34
  //   33 ff 37 35 34 33 ff 37 35 34 33 ff 37 35 34 33 ff 37 35 34 33 ff 37 35 34 33 ff 37 35 34 33 ff 37
  //   35 34 33 ff 37 35 34 33 ff 37 35 34 33 ff 37 35 34 33 ff 37 35 34 33 ff 37 35 34 33 ff 37 35 34 33
  //   ff 37 35 34 33 ff 37 35 34 33 ff 37 35 34 33 ff 37 35 34 33 ff 37 35 34 33 ff 37 35 34 33 ff 37 35
  //   34 33 ff 37 35 34 33 ff 37 35 34 33 ff 37 35 34 33 ff 37 35 34 33 ff 37 35 34 33 ff 37 35 34 33 ff
  //   37 35 34 33 ff 37 35 34 33 ff 37 35 34 33 ff 37 35 34 33 ff 37 35 34 33 ff 37 35 34 33 ff 37 35 34
  //   33 ff 37 35 34 33 ff 37 35 34 33 ff 37 35 34 33 ff 37 35 34 33 ff 37 35 34 33 ff 37 35 34 33 ff 37
  //   35 34 33 ff 37 35 34 33 ff 37 35 34 33 ff 37 35 34 33 ff 37 35 34 33 ff 37 35 34 33 ff 37 35 34 33
  //   ff 37 35 34 33 ff 37 35 34 33 ff 37 35 34 33 ff 37 35 34 33 ff 37 35 34 33 ff 37 35 34 33 ff 37 35
  //   34 33 ff 37 35 34 33 ff 37 35 34 33 ff 37 35 34 33 ff 37 35 34 33 ff 37 35 34 33 ff 37 35 34 33 ff
  //   37 35 34 33 ff 37 35 34 33 ff 37 35 34 33 ff 37 35 34 33 ff 37 35 34 33 ff 37 35 34 33 ff 37 35 34
  //   33 ff 37 35 34 33 ff 37 35 34 33 ff 37 35 34 33 ff 37 35 34 33 ff 37 35 34 33 ff 37 35 34 33 ff 37
  //   35 34 33 ff 37 35 34 33 ff 37 35 34 33 ff 37 35 34 33 ff 37 35 34 33 ff 37 35 34 33 ff 37 35 34 33
  //   ff 37 35 34 33 ff 37 35 34 33 ff 37 35 34 33 ff 37 35 34 33 ff 37 35 34 33 ff 37 35 34 33 ff 37 35
  //   34 33 ff 37 35 34 33 ff 37 35 34 33 ff 37 35 34 33 ff 37 35 34 33 ff 37 35 34 33 ff 37 35 34 33 ff
  //   37 35 34 33 ff 37 35 34 33 ff 37 35 34 33 ff 37 35 34 33 ff 37 35 34 33 ff 37 35 34 33 ff 37 35 34
  //   33 ff 37 35 34 33 ff 37 35 34 33 ff 37 35 34 33 ff 37 35 34 33 ff 37 35 34 33 ff 37 35 34 33 ff 37
  //   35 34 33 ff 37 35 34 33 ff 37 35 34 33 ff 37 35 34 33 ff 37 35 34 33 ff 37 35 34 33 ff 37 35 34 33
  //   ff 37 35 34 33 ff 37 35 34 33 ff 37 35 34 33 ff 37 35 34 33 ff 37 35 34 33 ff 37 35 34 33 ff 37 35
  //   34 33 ff 37 35 34 33 ff 37 35 34 33 ff 37 35 34 33 ff 37 35 34 33 ff 37 35 34 33 ff 37 35 34 33 ff
  //   37 35 34 33 ff 37 35 34 33 ff 37 35 34 33 ff 37 35 34 33 ff 37 35 34 33 ff 37 35 34 33 ff 37 35 34
  //   33 ff 37 35 34 33 ff 37 35 34 33 ff 37 35 34 33 ff 37 35 34 33 ff 37 35 34 33 ff 37 35 34 33 ff 37
  //   35 34 33 ff 37 35 34 33 ff 37 35 34 33 ff 37 35 34 33 ff 37 35 34 33 ff 37 35 34 33 ff 37 35 34 33
  //   ff 37 35 34 33 ff 37 35 34 33 ff 37 35 34 33 ff 37 35 34 33 ff 37 35 34 33 ff 37 35 34 33 ff 37 35
  //   34 33 d 35 34 33 ff 37 35 34 33 ff 37 35 34 33 ff 37 31 35 34 33 ff 22 35 34 33 ff 17 35 34 33 c 35
  //   34 33 d 35 34 33 ff 21 17 31 35 34 33 ff 22 35 34 33 ff 17 35 34 33 c 35 34 33 d 35 34 33 ff 21 17
  //   35 34 33 c 35 34 33 d 35 34 33 ff 21 17 35 34 33 ff 21 35 34 33 ff 17 35 34 33 ff 37 35 34 33 ff 21
  //   32 35 34 33 ff 17 35 34 33 ff 21 32 35 34 33 ff 17 35 34 33 ff 21 32 35 34 33 ff 17 35 34 33 ff 21
  //   32 35 34 33 ff 17 35 34 33 ff 21 35 34 33 ff 17 35 34 33 ff 21 35 34 33 ff 17 35 34 33 ff 21 35 34
  //   33 ff 17 35 34 33 ff 21 35 34 33 ff 17 35 34 33 ff 37 35 34 33 ff 21 35 34 33 ff 22 b7 35 34 33 ff
  //   87 35 34 33 ff 21 35 34 33 ff 22 b7 35 34 33 ff 87 35 34 33 9 35 34 33 ff 22 35 34 33 ff 21 17 35 34
  //   33 ff 22 35 34 33 ff 21 17 35 34 33 c 35 34 33 d 35 34 33 ff 21 17 35 34 33 ff 21 17 35 34 33 c 35
  //   34 33 ff 21 35 34 33 ff 17 35 34 33 ff 21 35 34 33 ff 17 35 34 33 ff 21 35 34 33 ff 22 35 34 33 ff
  //   23 35 14 ff 17 35 34 33 ff 21 35 34 33 ff 23 35 14 ff 22 15 ff 17 35 34 33 ff 21 17 35 34 33 c 35 34
  //   33 d 35 34 33 ff 21 17 35 34 33 ff 21 35 34 33 c 35 34 33 ff 21 35 34 33 c 35 34 33 d 35 34 33 d 35
  //   34 33 ff 37 31 35 34 33 ff 22 35 34 33 ff 17 35 34 33 c 35 34 33 d 35 34 33 ff 21 17 31 35 34 33 ff
  //   22 35 34 33 ff 17 35 34 33 c 3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
endmodule

module _181 (
  input  in_1,
  input  in_2,
  output A_B,
  output A_B_2,
  output Cn_4,
  output P,
  output P_2,
  output G,
  output G_2
);

  wire and_1_out, and_3_out, and_4_out, and_5_out, and_6_out, and_7_out, and_8_out, and_9_out, and_10_out,
       and_11_out, and_12_out, and_13_out, and_14_out, and_15_out, and_16_out, and_17_out, and_18_out,
       and_19_out, and_20_out, and_21_out, and_22_out, and_23_out, and_24_out, and_25_out, and_26_out,
       and_27_out, and_28_out, and_29_out, and_30_out, and_31_out, and_32_out, and_34_out, and_36_out,
       and_37_out, and_38_out, and_39_out, and_40_out, and_41_out, and_42_out, and_43_out, and_44_out,
       and_45_out, and_46_out, and_47_out, and_48_out, and_49_out, and_50_out, and_51_out, and_52_out,
       and_53_out, and_54_out, and_55_out, and_56_out, and_57_out, and_58_out, and_59_out, and_60_out,
       and_61_out, and_62_out, and_63_out, and_64_out, M, nand_2_out, nand_3_out, nor_1_out, nor_3_out,
       nor_4_out, nor_5_out, nor_6_out, nor_7_out, nor_8_out, nor_9_out, nor_10_out, nor_11_out, nor_12_out,
       nor_13_out, nor_15_out, nor_16_out, nor_17_out, nor_18_out, nor_19_out, nor_20_out, nor_21_out,
       nor_22_out, nor_23_out, nor_24_out, nor_25_out, not_1_out, not_2_out, not_3_out, not_4_out, not_5_out,
       not_6_out, not_7_out, not_8_out, not_9_out, not_10_out, xor_2_out, xor_4_out, xor_6_out, xor_9_out,
       xor_11_out, xor_13_out;
  wire [3:0] A, B, register_2_q, register_3_q, xor_7_out, xor_14_out;
  wire [7:0] register_1_q;

  Register register_1 (.Q({register_1_q[7:4], M, register_1_q[2:0]}));  // open: D, en, clk, clr
  Register register_2 (.Q({A, register_2_q}));  // open: D, en, clk, clr
  Register register_3 (.Q({B, register_3_q}));  // open: D, en, clk, clr
  Pull_Resistor #(.pull(1)) pull_resistor_1 (.node(A_B));
  and and_1 (and_1_out, P, G);
  nor nor_1 (nor_1_out, and_1_out, and_3_out);
  nor nor_2 (G, and_4_out, and_5_out, and_6_out, nor_4_out);
  and and_2 (A_B, xor_7_out[0], xor_7_out[1], xor_7_out[2], xor_7_out[3]);
  and and_3 (and_3_out, ~register_1_q[2], G);  // AND_Gate
  nand nand_1 (P, nor_11_out, nor_8_out, nor_5_out, nor_3_out);
  and and_4 (and_4_out, nor_13_out, nor_8_out, nor_5_out, nor_3_out);
  and and_5 (and_5_out, nor_9_out, nor_5_out, nor_3_out);
  and and_6 (and_6_out, nor_3_out, nor_7_out);
  and and_7 (and_7_out, register_3_q[3], register_1_q[7], register_2_q[3]);
  nor nor_3 (nor_3_out, and_7_out, and_8_out);
  and and_8 (and_8_out, register_1_q[6], register_2_q[3], not_1_out);
  and and_9 (and_9_out, not_1_out, register_1_q[5]);
  not not_1 (not_1_out, register_3_q[3]);
  nor nor_4 (nor_4_out, and_9_out, and_10_out, register_2_q[3]);
  and and_10 (and_10_out, register_1_q[4], register_3_q[3]);
  xor xor_1 (xor_7_out[3], xor_2_out, nor_6_out);
  xor xor_2 (xor_2_out, nor_3_out, nor_4_out);
  and and_11 (and_11_out, nor_5_out, nor_8_out, nor_11_out, register_1_q[2], not_5_out);
  nor nor_5 (nor_5_out, and_13_out, and_12_out);
  and and_12 (and_12_out, register_1_q[6], register_2_q[2], not_2_out);
  and and_13 (and_13_out, register_3_q[2], register_1_q[7], register_2_q[2]);
  nor nor_6 (nor_6_out, and_11_out, and_14_out, and_17_out, and_18_out);
  and and_14 (and_14_out, nor_13_out, nor_5_out, nor_8_out, not_5_out);
  nor nor_7 (nor_7_out, and_16_out, and_15_out, register_2_q[2]);
  and and_15 (and_15_out, register_1_q[4], register_3_q[2]);
  and and_16 (and_16_out, not_2_out, register_1_q[5]);
  not not_2 (not_2_out, register_3_q[2]);
  and and_17 (and_17_out, nor_9_out, nor_5_out, not_5_out);
  and and_18 (and_18_out, nor_7_out, not_5_out);
  nor nor_8 (nor_8_out, and_20_out, and_19_out);
  and and_19 (and_19_out, register_1_q[6], register_2_q[1], not_3_out);
  and and_20 (and_20_out, register_3_q[1], register_1_q[7], register_2_q[1]);
  xor xor_3 (xor_7_out[2], xor_4_out, nor_10_out);
  xor xor_4 (xor_4_out, nor_5_out, nor_7_out);
  and and_21 (and_21_out, nor_8_out, nor_11_out, register_1_q[2], not_5_out);
  nor nor_9 (nor_9_out, and_22_out, and_23_out, register_2_q[1]);
  and and_22 (and_22_out, not_3_out, register_1_q[5]);
  and and_23 (and_23_out, register_1_q[4], register_3_q[1]);
  not not_3 (not_3_out, register_3_q[1]);
  Register register_4 (.D({xor_14_out, xor_7_out}), .clk(in_1));  // open: en, Q, clr
  nor nor_10 (nor_10_out, and_21_out, and_25_out, and_24_out);
  and and_24 (and_24_out, nor_9_out, not_5_out);
  and and_25 (and_25_out, nor_13_out, nor_8_out, not_5_out);
  and and_26 (and_26_out, register_3_q[0], register_1_q[7], register_2_q[0]);
  xor xor_5 (xor_7_out[1], xor_6_out, nor_12_out);
  xor xor_6 (xor_6_out, nor_8_out, nor_9_out);
  and and_27 (and_27_out, nor_11_out, register_1_q[2], not_5_out);
  nor nor_11 (nor_11_out, and_26_out, and_28_out);
  and and_28 (and_28_out, register_1_q[6], register_2_q[0], not_4_out);
  and and_29 (and_29_out, not_4_out, register_1_q[5]);
  not not_4 (not_4_out, register_3_q[0]);
  and and_30 (and_30_out, nor_11_out, ~nor_13_out);  // AND_Gate
  nor nor_12 (nor_12_out, and_27_out, and_31_out);
  and and_31 (and_31_out, nor_13_out, not_5_out);
  nor nor_13 (nor_13_out, and_29_out, and_32_out, register_2_q[0]);
  and and_32 (and_32_out, register_1_q[4], register_3_q[0]);
  xor xor_7 (xor_7_out[0], and_30_out, nand_2_out);
  nand nand_2 (nand_2_out, register_1_q[2], not_5_out);
  not not_5 (not_5_out, M);
  or or_1 (Cn_4, ~G_2, ~and_34_out);  // OR_Gate
  Pull_Resistor #(.pull(1)) pull_resistor_2 (.node(A_B_2));
  nor nor_14 (G_2, and_36_out, and_37_out, and_38_out, nor_16_out);
  and and_33 (A_B_2, xor_14_out[0], xor_14_out[1], xor_14_out[2], xor_14_out[3]);
  and and_34 (and_34_out, nor_1_out, P_2);
  and and_35 (P_2, nor_23_out, nor_20_out, nor_17_out, nor_15_out);
  and and_36 (and_36_out, nor_25_out, nor_20_out, nor_17_out, nor_15_out);
  and and_37 (and_37_out, nor_22_out, nor_17_out, nor_15_out);
  and and_38 (and_38_out, nor_15_out, nor_19_out);
  nor nor_15 (nor_15_out, and_39_out, and_40_out);
  and and_39 (and_39_out, B[3], register_1_q[7], A[3]);
  and and_40 (and_40_out, register_1_q[6], A[3], not_6_out);
  and and_41 (and_41_out, not_6_out, register_1_q[5]);
  not not_6 (not_6_out, B[3]);
  xor xor_8 (xor_14_out[3], xor_9_out, nor_18_out);
  xor xor_9 (xor_9_out, nor_15_out, nor_16_out);
  nor nor_16 (nor_16_out, and_41_out, and_42_out, A[3]);
  and and_42 (and_42_out, register_1_q[4], B[3]);
  and and_43 (and_43_out, B[2], register_1_q[7], A[2]);
  and and_44 (and_44_out, nor_17_out, nor_20_out, nor_23_out, nor_1_out, not_10_out);
  nor nor_17 (nor_17_out, and_43_out, and_45_out);
  and and_45 (and_45_out, register_1_q[6], A[2], not_7_out);
  and and_46 (and_46_out, not_7_out, register_1_q[5]);
  not not_7 (not_7_out, B[2]);
  nor nor_18 (nor_18_out, and_44_out, and_47_out, and_48_out, and_50_out);
  and and_47 (and_47_out, nor_25_out, nor_17_out, nor_20_out, not_10_out);
  and and_48 (and_48_out, nor_22_out, nor_17_out, not_10_out);
  nor nor_19 (nor_19_out, and_46_out, and_49_out, A[2]);
  and and_49 (and_49_out, register_1_q[4], B[2]);
  xor xor_10 (xor_14_out[2], xor_11_out, nor_21_out);
  xor xor_11 (xor_11_out, nor_17_out, nor_19_out);
  and and_50 (and_50_out, nor_19_out, not_10_out);
  nor nor_20 (nor_20_out, and_51_out, and_52_out);
  and and_51 (and_51_out, B[1], register_1_q[7], A[1]);
  and and_52 (and_52_out, register_1_q[6], A[1], not_8_out);
  not not_8 (not_8_out, B[1]);
  nor nor_21 (nor_21_out, and_54_out, and_53_out, and_57_out);
  and and_53 (and_53_out, nor_25_out, nor_20_out, not_10_out);
  and and_54 (and_54_out, nor_20_out, nor_23_out, nor_1_out, not_10_out);
  nor nor_22 (nor_22_out, and_56_out, and_55_out, A[1]);
  and and_55 (and_55_out, register_1_q[4], B[1]);
  and and_56 (and_56_out, not_8_out, register_1_q[5]);
  and and_57 (and_57_out, nor_22_out, not_10_out);
  nor nor_23 (nor_23_out, and_59_out, and_58_out);
  and and_58 (and_58_out, register_1_q[6], A[0], not_9_out);
  and and_59 (and_59_out, B[0], register_1_q[7], A[0]);
  xor xor_12 (xor_14_out[1], xor_13_out, nor_24_out);
  xor xor_13 (xor_13_out, nor_20_out, nor_22_out);
  nor nor_24 (nor_24_out, and_60_out, and_64_out);
  and and_60 (and_60_out, nor_23_out, nor_1_out, not_10_out);
  nor nor_25 (nor_25_out, and_61_out, and_62_out, A[0]);
  and and_61 (and_61_out, not_9_out, register_1_q[5]);
  and and_62 (and_62_out, register_1_q[4], B[0]);
  not not_9 (not_9_out, B[0]);
  xor xor_14 (xor_14_out[0], and_63_out, nand_3_out);
  and and_63 (and_63_out, nor_23_out, ~nor_25_out);  // AND_Gate
  and and_64 (and_64_out, nor_25_out, not_10_out);
  nand nand_3 (nand_3_out, nor_1_out, not_10_out);
  not not_10 (not_10_out, M);
endmodule
